// Logisim project Lab2_Part2.circ as structural Verilog: 3 circuits, main circuit main
module main (
  input  SW_0,
  input  SW_1,
  input  SW_2,
  input  SW_3,
  input  SW_8,
  input  SW_9,
  output LEDR_0
);

  mux4to1 a (.u(SW_0), .v(SW_1), .w(SW_2), .x(SW_3), .s0(SW_8), .s1(SW_9), .m(LEDR_0));
endmodule

module mux2to1 (
  input  x,
  input  y,
  input  s,
  output m
);

  Multiplexer multiplexer_1 (.in0(x), .in1(y), .out(m), .sel(s));
endmodule

module mux4to1 (
  input  u,
  input  v,
  input  w,
  input  x,
  input  s0,
  input  s1,
  output m
);

  wire a_m, b_m;

  mux2to1 a (.x(u), .y(v), .s(s0), .m(a_m));
  mux2to1 b (.x(w), .y(x), .s(s0), .m(b_m));
  mux2to1 c (.x(a_m), .y(b_m), .s(s1), .m(m));
endmodule
