// Logisim project Lab2_Pat3.circ as structural Verilog: 9 circuits, main circuit main
module main (
  input  SW_0,
  input  SW_1,
  input  SW_2,
  input  SW_3
);

  wire a_hex0, b_hex1, c_hex2, d_hex3, e_hex4, f_hex5, g_hex6;

  Segment0 a (.c0(SW_0), .c1(SW_1), .c2(SW_2), .c3(SW_3), .HEX0(a_hex0));
  Segment2 c (.c0(SW_0), .c1(SW_1), .c2(SW_2), .c3(SW_3), .HEX2(c_hex2));
  Segment4 e (.c0(SW_0), .c1(SW_1), .c2(SW_2), .c3(SW_3), .HEX4(e_hex4));
  Segment6 g (.c0(SW_0), .c1(SW_1), .c2(SW_2), .c3(SW_3), .HEX6(g_hex6));
  _7_Segment_Display u_7_segment_display_1 (
    .g(g_hex6), .f(f_hex5), .a(a_hex0), .b(b_hex1), .e(e_hex4), .d(d_hex3), .c(c_hex2));  // open: dp
  Segment1 b (.c0(SW_0), .c1(SW_1), .c2(SW_2), .c3(SW_3), .HEX1(b_hex1));
  Segment3 d (.c0(SW_0), .c1(SW_1), .c2(SW_2), .c3(SW_3), .HEX3(d_hex3));
  Segment5 f (.c0(SW_0), .c1(SW_1), .c2(SW_2), .c3(SW_3), .HEX5(f_hex5));
endmodule

module Segment0 (
  input  c0,
  input  c1,
  input  c2,
  input  c3,
  output HEX0
);

  wire and_1_out, and_2_out, and_3_out, and_4_out, and_5_out, and_6_out, and_7_out, not_1_out, not_2_out,
       not_3_out, not_4_out;

  not not_1 (not_1_out, c0);
  not not_2 (not_2_out, c1);
  not not_3 (not_3_out, c2);
  not not_4 (not_4_out, c3);
  and and_1 (and_1_out, not_4_out, not_3_out, not_1_out);
  and and_2 (and_2_out, not_4_out, c2, c0);
  and and_3 (and_3_out, not_4_out, not_3_out, c1);
  and and_4 (and_4_out, c3, not_2_out, not_1_out);
  and and_5 (and_5_out, c3, c2, c1);
  and and_6 (and_6_out, c1, not_1_out);
  and and_7 (and_7_out, c3, not_3_out, not_2_out);
  or or_1 (HEX0, and_7_out, and_6_out, and_4_out, and_5_out, and_2_out, and_3_out, and_1_out);
endmodule

module Segment1 (
  input  c0,
  input  c1,
  input  c2,
  input  c3,
  output HEX1
);

  wire and_1_out, and_2_out, and_3_out, and_4_out, and_5_out, not_1_out, not_2_out, not_3_out, not_4_out;

  not not_1 (not_1_out, c0);
  not not_2 (not_2_out, c1);
  not not_3 (not_3_out, c2);
  not not_4 (not_4_out, c3);
  and and_1 (and_1_out, c3, not_2_out, c0);
  and and_2 (and_2_out, not_4_out, not_2_out, not_1_out);
  and and_3 (and_3_out, not_4_out, c1, c0);
  and and_4 (and_4_out, c3, not_3_out, not_1_out);
  and and_5 (and_5_out, not_4_out, not_3_out);
  or or_1 (HEX1, and_5_out, and_4_out, and_3_out, and_2_out, and_1_out);
endmodule

module Segment2 (
  input  c0,
  input  c1,
  input  c2,
  input  c3,
  output HEX2
);

  wire and_1_out, and_2_out, and_3_out, and_4_out, and_5_out, not_1_out, not_2_out, not_3_out, not_4_out;

  not not_1 (not_1_out, c0);
  not not_2 (not_2_out, c1);
  not not_3 (not_3_out, c2);
  not not_4 (not_4_out, c3);
  and and_1 (and_1_out, c2, not_2_out, c0);
  and and_2 (and_2_out, not_4_out, c1, c0);
  and and_3 (and_3_out, not_4_out, not_3_out, not_2_out);
  and and_4 (and_4_out, not_4_out, c2, not_1_out);
  and and_5 (and_5_out, c3, not_3_out);
  or or_1 (HEX2, and_5_out, and_4_out, and_3_out, and_2_out, and_1_out);
endmodule

module Segment3 (
  input  c0,
  input  c1,
  input  c2,
  input  c3,
  output HEX3
);

  wire and_1_out, and_2_out, and_3_out, and_4_out, and_5_out, not_1_out, not_2_out, not_3_out, not_4_out;

  not not_1 (not_1_out, c0);
  not not_2 (not_2_out, c1);
  not not_3 (not_3_out, c2);
  not not_4 (not_4_out, c3);
  and and_1 (and_1_out, c2, not_2_out, c0);
  and and_2 (and_2_out, not_3_out, c1, c0);
  and and_3 (and_3_out, c2, c1, not_1_out);
  and and_4 (and_4_out, not_4_out, not_3_out, not_1_out);
  and and_5 (and_5_out, c3, not_2_out);
  or or_1 (HEX3, and_5_out, and_4_out, and_3_out, and_2_out, and_1_out);
endmodule

module Segment4 (
  input  c0,
  input  c1,
  input  c2,
  input  c3,
  output HEX4
);

  wire and_1_out, and_2_out, and_3_out, and_4_out, not_1_out, not_2_out, not_3_out, not_4_out;

  not not_1 (not_1_out, c0);
  not not_2 (not_2_out, c1);
  not not_3 (not_3_out, c2);
  not not_4 (not_4_out, c3);
  and and_1 (and_1_out, not_3_out, not_2_out, not_1_out);
  and and_2 (and_2_out, not_4_out, c1, not_1_out);
  and and_3 (and_3_out, c3, not_3_out, c1);
  and and_4 (and_4_out, c3, c2);
  or or_1 (HEX4, and_4_out, and_3_out, and_2_out, and_1_out);
endmodule

module Segment5 (
  input  c0,
  input  c1,
  input  c2,
  input  c3,
  output HEX5
);

  wire and_1_out, and_2_out, and_3_out, and_4_out, and_5_out, not_1_out, not_2_out, not_3_out, not_4_out;

  not not_1 (not_1_out, c0);
  not not_2 (not_2_out, c1);
  not not_3 (not_3_out, c2);
  not not_4 (not_4_out, c3);
  and and_1 (and_1_out, not_2_out, not_1_out);
  and and_2 (and_2_out, c2, c1, not_1_out);
  and and_3 (and_3_out, not_4_out, c2, not_2_out);
  and and_4 (and_4_out, c3, c2, c1);
  and and_5 (and_5_out, c3, not_3_out);
  or or_1 (HEX5, and_5_out, and_4_out, and_3_out, and_2_out, and_1_out);
endmodule

module Segment6 (
  input  c0,
  input  c1,
  input  c2,
  input  c3,
  output HEX6
);

  wire and_1_out, and_2_out, and_3_out, and_4_out, and_5_out, not_1_out, not_2_out, not_3_out, not_4_out;

  not not_1 (not_1_out, c0);
  not not_2 (not_2_out, c1);
  not not_3 (not_3_out, c2);
  not not_4 (not_4_out, c3);
  and and_1 (and_1_out, c2, c1, not_1_out);
  and and_2 (and_2_out, not_4_out, not_3_out, c1);
  and and_3 (and_3_out, not_4_out, c2, not_2_out);
  and and_4 (and_4_out, c3, c2, c0);
  and and_5 (and_5_out, c3, not_3_out);
  or or_1 (HEX6, and_5_out, and_4_out, and_3_out, and_2_out, and_1_out);
endmodule

module Display (
  input  c0,
  input  c1,
  input  c2,
  input  c3
);

  wire a_hex0, b_hex1, c_hex2, d_hex3, e_hex4, f_hex5, g_hex6;

  Segment0 a (.c0(c0), .c1(c1), .c2(c2), .c3(c3), .HEX0(a_hex0));
  Segment2 c (.c0(c0), .c1(c1), .c2(c2), .c3(c3), .HEX2(c_hex2));
  Segment4 e (.c0(c0), .c1(c1), .c2(c2), .c3(c3), .HEX4(e_hex4));
  Segment6 g (.c0(c0), .c1(c1), .c2(c2), .c3(c3), .HEX6(g_hex6));
  _7_Segment_Display u_7_segment_display_1 (
    .g(g_hex6), .f(f_hex5), .a(a_hex0), .b(b_hex1), .e(e_hex4), .d(d_hex3), .c(c_hex2));  // open: dp
  Segment1 b (.c0(c0), .c1(c1), .c2(c2), .c3(c3), .HEX1(b_hex1));
  Segment3 d (.c0(c0), .c1(c1), .c2(c2), .c3(c3), .HEX3(d_hex3));
  Segment5 f (.c0(c0), .c1(c1), .c2(c2), .c3(c3), .HEX5(f_hex5));
endmodule
