// Logisim project lab3_part2.circ as structural Verilog: 3 circuits, main circuit main
module main (
  input  [3:0] A,
  input  c_in,
  input  [3:0] B,
  output c_out,
  output [3:0] S
);

  ripple_carry_adder ripple_carry (.A(A), .c_in(c_in), .B(B), .c_out(c_out), .S(S));
endmodule

module full_adder (
  input  c_i,
  input  a,
  input  b,
  output s,
  output c_o
);

  wire xor_1_out;

  xor xor_1 (xor_1_out, a, b);
  Multiplexer multiplexer_1 (.in0(b), .in1(c_i), .out(c_o), .sel(xor_1_out));
  xor xor_2 (s, c_i, xor_1_out);
endmodule

module ripple_carry_adder (
  input  [3:0] A,
  input  c_in,
  input  [3:0] B,
  output c_out,
  output [3:0] S
);

  wire f1_c_o, f2_c_o, f3_c_o;

  full_adder f4 (.c_i(f3_c_o), .a(A[3]), .b(B[3]), .s(S[3]), .c_o(c_out));
  full_adder f3 (.c_i(f2_c_o), .a(A[2]), .b(B[2]), .s(S[2]), .c_o(f3_c_o));
  full_adder f2 (.c_i(f1_c_o), .a(A[1]), .b(B[1]), .s(S[1]), .c_o(f2_c_o));
  full_adder f1 (.c_i(c_in), .a(A[0]), .b(B[0]), .s(S[0]), .c_o(f1_c_o));
endmodule
