// Logisim project lab4_part2.circ as structural Verilog: 20 circuits, main circuit main
module main (
  input  [3:0] A,
  input  [2:0] function_value,
  input  Clk,
  output [7:0] ALU_output
);

  wire [7:0] alu_1_alu_output;

  Hex_Digit_Display hex_digit_display_1 (.value(A));  // open: dp
  Register register_1 (.D(alu_1_alu_output), .clk(Clk), .Q(ALU_output));  // open: en, clr
  ALU alu_1 (.A(A), .B(ALU_output[3:0]), .function_value(function_value), .ALU_output(alu_1_alu_output));
  LED led_1 (.in(ALU_output[7]));
  LED led_2 (.in(ALU_output[6]));
  LED led_3 (.in(ALU_output[5]));
  LED led_4 (.in(ALU_output[4]));
  LED led_5 (.in(ALU_output[3]));
  LED led_6 (.in(ALU_output[2]));
  LED led_7 (.in(ALU_output[1]));
  LED led_8 (.in(ALU_output[0]));
  Hex_Digit_Display hex_digit_display_2 (.value(ALU_output[7:4]));  // open: dp
  Hex_Digit_Display hex_digit_display_3 (.value(ALU_output[3:0]));  // open: dp
endmodule

module ALU (
  input  [3:0] A,
  input  [3:0] B,
  input  [2:0] function_value,
  output [7:0] ALU_output
);

  wire [7:0] f0_alu_out, f1_alu_out, f2_alu_out, f3_alu_out, f4_alu_out, f5_alu_out, function6_1_alu_out,
       function7_1_alu_out;

  function0 f0 (.A(A), .ALU_out(f0_alu_out));
  function1 f1 (.A(A), .B(B), .ALU_out(f1_alu_out));
  function2 f2 (.A(A), .B(B), .ALU_out(f2_alu_out));
  function3 f3 (.A(A), .B(B), .ALU_out(f3_alu_out));
  function4 f4 (.A(A), .B(B), .ALU_out(f4_alu_out));
  function5 f5 (.B(B), .A(A), .ALU_out(f5_alu_out));
  function6 function6_1 (.B(B), .A(A), .ALU_out(function6_1_alu_out));
  function7 function7_1 (.A(A), .B(B), .ALU_out(function7_1_alu_out));
  Multiplexer #(.select(3), .width(8)) multiplexer_1 (
    .in0(f0_alu_out), .in1(f1_alu_out), .in2(f2_alu_out), .in3(f3_alu_out), .in4(f4_alu_out),
    .in5(f5_alu_out), .in6(function6_1_alu_out), .in7(function7_1_alu_out), .out(ALU_output),
    .sel(function_value));
endmodule

module seven_decoder (
  input  SW_0,
  input  SW_1,
  input  SW_2,
  input  SW_3,
  output HEX0,
  output HEX1,
  output HEX2,
  output HEX3,
  output HEX4,
  output HEX5,
  output HEX6
);

  Segment0 a (.c0(SW_0), .c1(SW_1), .c2(SW_2), .c3(SW_3), .HEX0(HEX0));
  Segment2 c (.c0(SW_0), .c1(SW_1), .c2(SW_2), .c3(SW_3), .HEX2(HEX2));
  Segment4 e (.c0(SW_0), .c1(SW_1), .c2(SW_2), .c3(SW_3), .HEX4(HEX4));
  Segment6 g (.c0(SW_0), .c1(SW_1), .c2(SW_2), .c3(SW_3), .HEX6(HEX6));
  Segment1 b (.c0(SW_0), .c1(SW_1), .c2(SW_2), .c3(SW_3), .HEX1(HEX1));
  Segment3 d (.c0(SW_0), .c1(SW_1), .c2(SW_2), .c3(SW_3), .HEX3(HEX3));
  Segment5 f (.c0(SW_0), .c1(SW_1), .c2(SW_2), .c3(SW_3), .HEX5(HEX5));
endmodule

module Segment0 (
  input  c0,
  input  c1,
  input  c2,
  input  c3,
  output HEX0
);

  wire and_1_out, and_2_out, and_3_out, and_4_out, and_5_out, and_6_out, and_7_out, not_1_out, not_2_out,
       not_3_out, not_4_out;

  not not_1 (not_1_out, c0);
  not not_2 (not_2_out, c1);
  not not_3 (not_3_out, c2);
  not not_4 (not_4_out, c3);
  and and_1 (and_1_out, not_4_out, not_3_out, not_1_out);
  and and_2 (and_2_out, not_4_out, c2, c0);
  and and_3 (and_3_out, not_4_out, not_3_out, c1);
  and and_4 (and_4_out, c3, not_2_out, not_1_out);
  and and_5 (and_5_out, c3, c2, c1);
  and and_6 (and_6_out, c1, not_1_out);
  and and_7 (and_7_out, c3, not_3_out, not_2_out);
  or or_1 (HEX0, and_7_out, and_6_out, and_4_out, and_5_out, and_2_out, and_3_out, and_1_out);
endmodule

module Segment1 (
  input  c0,
  input  c1,
  input  c2,
  input  c3,
  output HEX1
);

  wire and_1_out, and_2_out, and_3_out, and_4_out, and_5_out, not_1_out, not_2_out, not_3_out, not_4_out;

  not not_1 (not_1_out, c0);
  not not_2 (not_2_out, c1);
  not not_3 (not_3_out, c2);
  not not_4 (not_4_out, c3);
  and and_1 (and_1_out, c3, not_2_out, c0);
  and and_2 (and_2_out, not_4_out, not_2_out, not_1_out);
  and and_3 (and_3_out, not_4_out, c1, c0);
  and and_4 (and_4_out, c3, not_3_out, not_1_out);
  and and_5 (and_5_out, not_4_out, not_3_out);
  or or_1 (HEX1, and_5_out, and_4_out, and_3_out, and_2_out, and_1_out);
endmodule

module Segment2 (
  input  c0,
  input  c1,
  input  c2,
  input  c3,
  output HEX2
);

  wire and_1_out, and_2_out, and_3_out, and_4_out, and_5_out, not_1_out, not_2_out, not_3_out, not_4_out;

  not not_1 (not_1_out, c0);
  not not_2 (not_2_out, c1);
  not not_3 (not_3_out, c2);
  not not_4 (not_4_out, c3);
  and and_1 (and_1_out, c2, not_2_out, c0);
  and and_2 (and_2_out, not_4_out, c1, c0);
  and and_3 (and_3_out, not_4_out, not_3_out, not_2_out);
  and and_4 (and_4_out, not_4_out, c2, not_1_out);
  and and_5 (and_5_out, c3, not_3_out);
  or or_1 (HEX2, and_5_out, and_4_out, and_3_out, and_2_out, and_1_out);
endmodule

module Segment3 (
  input  c0,
  input  c1,
  input  c2,
  input  c3,
  output HEX3
);

  wire and_1_out, and_2_out, and_3_out, and_4_out, and_5_out, not_1_out, not_2_out, not_3_out, not_4_out;

  not not_1 (not_1_out, c0);
  not not_2 (not_2_out, c1);
  not not_3 (not_3_out, c2);
  not not_4 (not_4_out, c3);
  and and_1 (and_1_out, c2, not_2_out, c0);
  and and_2 (and_2_out, not_3_out, c1, c0);
  and and_3 (and_3_out, c2, c1, not_1_out);
  and and_4 (and_4_out, not_4_out, not_3_out, not_1_out);
  and and_5 (and_5_out, c3, not_2_out);
  or or_1 (HEX3, and_5_out, and_4_out, and_3_out, and_2_out, and_1_out);
endmodule

module Segment4 (
  input  c0,
  input  c1,
  input  c2,
  input  c3,
  output HEX4
);

  wire and_1_out, and_2_out, and_3_out, and_4_out, not_1_out, not_2_out, not_3_out, not_4_out;

  not not_1 (not_1_out, c0);
  not not_2 (not_2_out, c1);
  not not_3 (not_3_out, c2);
  not not_4 (not_4_out, c3);
  and and_1 (and_1_out, not_3_out, not_2_out, not_1_out);
  and and_2 (and_2_out, not_4_out, c1, not_1_out);
  and and_3 (and_3_out, c3, not_3_out, c1);
  and and_4 (and_4_out, c3, c2);
  or or_1 (HEX4, and_4_out, and_3_out, and_2_out, and_1_out);
endmodule

module Segment5 (
  input  c0,
  input  c1,
  input  c2,
  input  c3,
  output HEX5
);

  wire and_1_out, and_2_out, and_3_out, and_4_out, and_5_out, not_1_out, not_2_out, not_3_out, not_4_out;

  not not_1 (not_1_out, c0);
  not not_2 (not_2_out, c1);
  not not_3 (not_3_out, c2);
  not not_4 (not_4_out, c3);
  and and_1 (and_1_out, not_2_out, not_1_out);
  and and_2 (and_2_out, c2, c1, not_1_out);
  and and_3 (and_3_out, not_4_out, c2, not_2_out);
  and and_4 (and_4_out, c3, c2, c1);
  and and_5 (and_5_out, c3, not_3_out);
  or or_1 (HEX5, and_5_out, and_4_out, and_3_out, and_2_out, and_1_out);
endmodule

module Segment6 (
  input  c0,
  input  c1,
  input  c2,
  input  c3,
  output HEX6
);

  wire and_1_out, and_2_out, and_3_out, and_4_out, and_5_out, not_1_out, not_2_out, not_3_out, not_4_out;

  not not_1 (not_1_out, c0);
  not not_2 (not_2_out, c1);
  not not_3 (not_3_out, c2);
  not not_4 (not_4_out, c3);
  and and_1 (and_1_out, c2, c1, not_1_out);
  and and_2 (and_2_out, not_4_out, not_3_out, c1);
  and and_3 (and_3_out, not_4_out, c2, not_2_out);
  and and_4 (and_4_out, c3, c2, c0);
  and and_5 (and_5_out, c3, not_3_out);
  or or_1 (HEX6, and_5_out, and_4_out, and_3_out, and_2_out, and_1_out);
endmodule

module full_adder (
  input  c_i,
  input  a,
  input  b,
  output s,
  output c_o
);

  wire xor_1_out;

  xor xor_1 (xor_1_out, a, b);
  Multiplexer multiplexer_1 (.in0(b), .in1(c_i), .out(c_o), .sel(xor_1_out));
  xor xor_2 (s, c_i, xor_1_out);
endmodule

module ripple_carry_adder (
  input  [3:0] A,
  input  c_in,
  input  [3:0] B,
  output c_out,
  output [3:0] S
);

  wire f1_c_o, f2_c_o, f3_c_o;

  full_adder f4 (.c_i(f3_c_o), .a(A[3]), .b(B[3]), .s(S[3]), .c_o(c_out));
  full_adder f3 (.c_i(f2_c_o), .a(A[2]), .b(B[2]), .s(S[2]), .c_o(f3_c_o));
  full_adder f2 (.c_i(f1_c_o), .a(A[1]), .b(B[1]), .s(S[1]), .c_o(f2_c_o));
  full_adder f1 (.c_i(c_in), .a(A[0]), .b(B[0]), .s(S[0]), .c_o(f1_c_o));
endmodule

module function0 (
  input  [3:0] A,
  output [7:0] ALU_out
);

  wire ripple_carry_adder_1_c_out;

  ripple_carry_adder ripple_carry_adder_1 (
    .A(A), .c_in(1'b1), .B(4'b0000), .c_out(ripple_carry_adder_1_c_out), .S(ALU_out[3:0]));
  assign ALU_out[7:4] = {{3{1'b0}}, ripple_carry_adder_1_c_out};  // Bit_Extender bit_extender_1
endmodule

module function1 (
  input  [3:0] A,
  input  [3:0] B,
  output [7:0] ALU_out
);

  wire ripple_carry_adder_1_c_out;

  ripple_carry_adder ripple_carry_adder_1 (
    .A(A), .c_in(1'b0), .B(B), .c_out(ripple_carry_adder_1_c_out), .S(ALU_out[3:0]));
  assign ALU_out[7:4] = {{3{1'b0}}, ripple_carry_adder_1_c_out};  // Bit_Extender bit_extender_1
endmodule

module function2 (
  input  [3:0] A,
  input  [3:0] B,
  output [7:0] ALU_out
);

  wire adder_1_cout;

  Adder #(.width(4)) adder_1 (.a(A), .b(B), .out(ALU_out[3:0]), .cin(1'b0), .cout(adder_1_cout));
  assign ALU_out[7:4] = {{3{1'b0}}, adder_1_cout};  // Bit_Extender bit_extender_1
endmodule

module function3 (
  input  [3:0] A,
  input  [3:0] B,
  output [7:0] ALU_out
);

  xor xor_1 (ALU_out[0], A[0], B[0]);
  xor xor_2 (ALU_out[1], B[1], A[1]);
  xor xor_3 (ALU_out[2], B[2], A[2]);
  xor xor_4 (ALU_out[3], B[3], A[3]);
  or or_1 (ALU_out[4], B[0], A[0]);
  or or_2 (ALU_out[5], B[1], A[1]);
  or or_3 (ALU_out[6], B[2], A[2]);
  or or_4 (ALU_out[7], B[3], A[3]);
endmodule

module function4 (
  input  [3:0] A,
  input  [3:0] B,
  output [7:0] ALU_out
);

  wire or_1_out;

  or or_1 (or_1_out, A[0], A[1], A[2], A[3], B[0], B[1], B[2], B[3]);
  assign ALU_out = {{7{1'b0}}, or_1_out};  // Bit_Extender bit_extender_1
endmodule

module function5 (
  input  [3:0] B,
  input  [3:0] A,
  output [7:0] ALU_out
);

  wire [8:0] bit_extender_1_out;
  wire [8:8] shifter_1_out;

  assign bit_extender_1_out = {{5{1'b0}}, B};  // Bit_Extender bit_extender_1
  Shifter #(.width(9)) shifter_1 (.in(bit_extender_1_out), .\dist (A), .out({shifter_1_out[8], ALU_out}));
endmodule

module function6 (
  input  [3:0] B,
  input  [3:0] A,
  output [7:0] ALU_out
);

  wire [8:0] bit_extender_1_out;
  wire [8:8] shifter_1_out;

  assign bit_extender_1_out = {{5{1'b0}}, B};  // Bit_Extender bit_extender_1
  Shifter #(.shift("lr"), .width(9)) shifter_1 (.in(bit_extender_1_out), .\dist (A), .out({shifter_1_out[8], ALU_out}));
endmodule

module function7 (
  input  [3:0] A,
  input  [3:0] B,
  output [7:0] ALU_out
);

  Multiplier #(.width(4)) multiplier_1 (.a(A), .b(B), .out(ALU_out[3:0]), .cout(ALU_out[7:4]));  // open: cin
endmodule
