// Logisim project lab5_part2.circ as structural Verilog: 15 circuits, main circuit main
module main (
  input  enable,
  input  clear,
  input  [1:0] SW
);

  wire Clk_out, hexdecoder_1_s0, hexdecoder_1_s1, hexdecoder_1_s2, hexdecoder_1_s3, hexdecoder_1_s4,
       hexdecoder_1_s5, hexdecoder_1_s6;
  wire [3:0] connectcounters_1_counter_out;

  Clock Clk (.out(Clk_out));
  ConnectCounters connectcounters_1 (
    .enable(enable), .clear(clear), .Clk(Clk_out), .SW(SW), .counter_out(connectcounters_1_counter_out));
  HexDecoder hexdecoder_1 (
    .SW_3(connectcounters_1_counter_out[3]), .SW_2(connectcounters_1_counter_out[2]),
    .SW_1(connectcounters_1_counter_out[1]), .SW_0(connectcounters_1_counter_out[0]), .S0(hexdecoder_1_s0),
    .S1(hexdecoder_1_s1), .S2(hexdecoder_1_s2), .S3(hexdecoder_1_s3), .S4(hexdecoder_1_s4),
    .S5(hexdecoder_1_s5), .S6(hexdecoder_1_s6));
  _7_Segment_Display u_7_segment_display_1 (
    .g(hexdecoder_1_s6), .f(hexdecoder_1_s5), .a(hexdecoder_1_s0), .b(hexdecoder_1_s1), .e(hexdecoder_1_s4),
    .d(hexdecoder_1_s3), .c(hexdecoder_1_s2));  // open: dp
endmodule

module ConnectCounters (
  input  enable,
  input  clear,
  input  Clk,
  input  [1:0] SW,
  output [3:0] counter_out
);

  wire not_1_out, ratedivider_1_divider_out;

  not not_1 (not_1_out, Clk);
  RateDivider ratedivider_1 (
    .enable(enable), .clear(clear), .Clk(not_1_out), .SW(SW), .divider_out(ratedivider_1_divider_out));
  DisplayCounter displaycounter_1 (
    .clear(clear), .enable(ratedivider_1_divider_out), .Clk(Clk), .counter_out(counter_out));
endmodule

module RateDivider (
  input  enable,
  input  clear,
  input  Clk,
  input  [1:0] SW,
  output divider_out
);

  wire halfhz_1_counter_out, onehz_1_counter_out, quarterhz_1_counter_out;

  oneHz onehz_1 (.enable(enable), .clear(clear), .Clk(Clk), .counter_out(onehz_1_counter_out));
  halfHz halfhz_1 (.enable(enable), .clear(clear), .Clk(Clk), .counter_out(halfhz_1_counter_out));
  quarterHz quarterhz_1 (.enable(enable), .clear(clear), .Clk(Clk), .counter_out(quarterhz_1_counter_out));
  Multiplexer #(.select(2)) multiplexer_1 (
    .in0(Clk), .in1(onehz_1_counter_out), .in2(halfhz_1_counter_out), .in3(quarterhz_1_counter_out),
    .out(divider_out), .sel(SW));
endmodule

module DisplayCounter (
  input  clear,
  input  enable,
  input  Clk,
  output [3:0] counter_out
);

  wire not_1_out;

  not not_1 (not_1_out, enable);
  Counter #(.max('hf), .width(4)) counter_1 (
    .clr(clear), .load(not_1_out), .up(1'b1), .clk(Clk), .D(counter_out), .Q(counter_out));  // open: count, carry
endmodule

module oneHz (
  input  enable,
  input  clear,
  input  Clk,
  output counter_out
);

  wire not_1_out, or_1_out;
  wire [3:0] counter_1_q;

  not not_1 (not_1_out, enable);
  or or_1 (or_1_out, counter_out, not_1_out);
  Counter #(.max('hf), .width(4)) counter_1 (
    .clr(clear), .load(or_1_out), .up(1'b1), .clk(Clk), .D(4'b0000), .Q(counter_1_q));  // open: count, carry
  and and_1 (counter_out, counter_1_q[0], counter_1_q[1], counter_1_q[2], counter_1_q[3]);
endmodule

module halfHz (
  input  enable,
  input  clear,
  input  Clk,
  output counter_out
);

  wire not_1_out, or_1_out;
  wire [4:0] counter_1_q;

  or or_1 (or_1_out, counter_out, not_1_out);
  not not_1 (not_1_out, enable);
  Counter #(.max('h1f), .width(5)) counter_1 (
    .clr(clear), .load(or_1_out), .up(1'b1), .clk(Clk), .D({5{1'b0}}), .Q(counter_1_q));  // open: count, carry
  and and_1 (counter_out, counter_1_q[0], counter_1_q[1], counter_1_q[2], counter_1_q[3], counter_1_q[4]);
endmodule

module quarterHz (
  input  enable,
  input  clear,
  input  Clk,
  output counter_out
);

  wire not_1_out, or_1_out;
  wire [5:0] counter_1_q;

  or or_1 (or_1_out, counter_out, not_1_out);
  not not_1 (not_1_out, enable);
  Counter #(.max('h3f), .width(6)) counter_1 (
    .clr(clear), .load(or_1_out), .up(1'b1), .clk(Clk), .D({6{1'b0}}), .Q(counter_1_q));  // open: count, carry
  and and_1 (counter_out, counter_1_q[0], counter_1_q[1], counter_1_q[2], counter_1_q[3], counter_1_q[4], counter_1_q[5]);
endmodule

module HexDecoder (
  input  SW_3,
  input  SW_2,
  input  SW_1,
  input  SW_0,
  output S0,
  output S1,
  output S2,
  output S3,
  output S4,
  output S5,
  output S6
);

  Segment0 Hex0 (.c_3(SW_3), .c_2(SW_2), .c_1(SW_1), .c_0(SW_0), .Hex0(S0));
  Segment1 Hex1 (.c_3(SW_3), .c_2(SW_2), .c_1(SW_1), .c_0(SW_0), .Hex1(S1));
  Segment2 Hex2 (.c_3(SW_3), .c_2(SW_2), .c_1(SW_1), .c_0(SW_0), .Hex2(S2));
  Segment3 Hex3 (.c_3(SW_3), .c_2(SW_2), .c_1(SW_1), .c_0(SW_0), .Hex3(S3));
  Segment4 Hex4 (.c_3(SW_3), .c_2(SW_2), .c_1(SW_1), .c_0(SW_0), .Hex4(S4));
  Segment5 Hex5 (.c_3(SW_3), .c_2(SW_2), .c_1(SW_1), .c_0(SW_0), .Hex5(S5));
  Segment6 Hex6 (.c_3(SW_3), .c_2(SW_2), .c_1(SW_1), .c_0(SW_0), .Hex6(S6));
endmodule

module Segment0 (
  input  c_3,
  input  c_2,
  input  c_1,
  input  c_0,
  output Hex0
);

  wire and_1_out, and_2_out, and_3_out, and_4_out, and_5_out, and_6_out, not_1_out, not_2_out, not_3_out,
       not_4_out, not_5_out;

  not not_1 (not_1_out, c_0);
  not not_2 (not_2_out, c_3);
  not not_3 (not_3_out, c_2);
  not not_4 (not_4_out, c_0);
  not not_5 (not_5_out, c_1);
  and and_1 (and_1_out, c_3, not_1_out);
  and and_2 (and_2_out, not_2_out, c_1);
  and and_3 (and_3_out, not_3_out, not_4_out);
  and and_4 (and_4_out, c_1, c_2);
  and and_5 (and_5_out, not_2_out, c_2, c_0);
  and and_6 (and_6_out, c_3, not_3_out, not_5_out);
  or or_1 (Hex0, and_1_out, and_2_out, and_3_out, and_4_out, and_5_out, and_6_out);
endmodule

module Segment1 (
  input  c_3,
  input  c_2,
  input  c_1,
  input  c_0,
  output Hex1
);

  wire and_1_out, and_2_out, and_3_out, and_4_out, and_5_out, not_1_out, not_2_out, not_3_out, not_4_out;

  not not_1 (not_1_out, c_3);
  not not_2 (not_2_out, c_2);
  not not_3 (not_3_out, c_1);
  not not_4 (not_4_out, c_0);
  and and_1 (and_1_out, not_2_out, not_4_out);
  and and_2 (and_2_out, not_1_out, not_2_out);
  and and_3 (and_3_out, not_1_out, not_3_out, not_4_out);
  and and_4 (and_4_out, c_3, not_3_out, c_0);
  and and_5 (and_5_out, not_1_out, c_1, c_0);
  or or_1 (Hex1, and_1_out, and_2_out, and_3_out, and_4_out, and_5_out);
endmodule

module Segment2 (
  input  c_3,
  input  c_2,
  input  c_1,
  input  c_0,
  output Hex2
);

  wire and_1_out, and_2_out, and_3_out, and_4_out, and_5_out, not_1_out, not_2_out, not_3_out;

  not not_1 (not_1_out, c_3);
  not not_2 (not_2_out, c_2);
  not not_3 (not_3_out, c_1);
  and and_1 (and_1_out, not_1_out, not_3_out);
  and and_2 (and_2_out, not_1_out, c_0);
  and and_3 (and_3_out, c_3, not_2_out);
  and and_4 (and_4_out, not_1_out, c_2);
  and and_5 (and_5_out, not_3_out, c_0);
  or or_1 (Hex2, and_1_out, and_2_out, and_3_out, and_4_out, and_5_out);
endmodule

module Segment3 (
  input  c_3,
  input  c_2,
  input  c_1,
  input  c_0,
  output Hex3
);

  wire and_1_out, and_2_out, and_3_out, and_4_out, and_5_out, not_1_out, not_2_out, not_3_out, not_4_out;

  not not_1 (not_1_out, c_3);
  not not_2 (not_2_out, c_2);
  not not_3 (not_3_out, c_1);
  not not_4 (not_4_out, c_0);
  and and_1 (and_1_out, not_1_out, not_2_out, not_4_out);
  and and_2 (and_2_out, c_3, not_3_out, not_4_out);
  and and_3 (and_3_out, c_2, not_3_out, c_0);
  and and_4 (and_4_out, not_2_out, c_1, c_0);
  and and_5 (and_5_out, c_2, c_1, not_4_out);
  or or_1 (Hex3, and_1_out, and_2_out, and_3_out, and_4_out, and_5_out);
endmodule

module Segment4 (
  input  c_3,
  input  c_2,
  input  c_1,
  input  c_0,
  output Hex4
);

  wire and_1_out, and_2_out, and_3_out, and_4_out, not_1_out, not_2_out;

  not not_1 (not_1_out, c_2);
  not not_2 (not_2_out, c_0);
  and and_1 (and_1_out, c_3, c_2);
  and and_2 (and_2_out, c_1, not_2_out);
  and and_3 (and_3_out, not_1_out, not_2_out);
  and and_4 (and_4_out, c_3, c_1);
  or or_1 (Hex4, and_1_out, and_2_out, and_3_out, and_4_out);
endmodule

module Segment5 (
  input  c_3,
  input  c_2,
  input  c_1,
  input  c_0,
  output Hex5
);

  wire and_1_out, and_2_out, and_3_out, and_4_out, and_5_out, not_1_out, not_2_out, not_3_out, not_4_out;

  not not_1 (not_1_out, c_3);
  not not_2 (not_2_out, c_2);
  not not_3 (not_3_out, c_1);
  not not_4 (not_4_out, c_0);
  and and_1 (and_1_out, not_3_out, not_4_out);
  and and_2 (and_2_out, c_3, not_2_out);
  and and_3 (and_3_out, not_1_out, c_2, not_3_out);
  and and_4 (and_4_out, c_3, c_2, c_1);
  and and_5 (and_5_out, c_2, c_1, not_4_out);
  or or_1 (Hex5, and_1_out, and_2_out, and_3_out, and_4_out, and_5_out);
endmodule

module Segment6 (
  input  c_3,
  input  c_2,
  input  c_1,
  input  c_0,
  output Hex6
);

  wire and_1_out, and_2_out, and_3_out, and_4_out, and_5_out, and_6_out, not_1_out, not_2_out, not_3_out,
       not_4_out;

  not not_1 (not_1_out, c_3);
  not not_2 (not_2_out, c_2);
  not not_3 (not_3_out, c_1);
  not not_4 (not_4_out, c_0);
  and and_1 (and_1_out, c_3, not_2_out);
  and and_2 (and_2_out, c_1, not_4_out);
  and and_3 (and_3_out, c_3, c_0);
  and and_4 (and_4_out, c_3, c_1);
  and and_5 (and_5_out, not_1_out, c_2, not_3_out);
  and and_6 (and_6_out, not_1_out, not_2_out, c_1);
  or or_1 (Hex6, and_1_out, and_2_out, and_3_out, and_4_out, and_5_out, and_6_out);
endmodule
