// Logisim project lab5_part3.circ as structural Verilog: 4 circuits, main circuit LUT
module main (
  input  KEY1,
  input  KEY0,
  input  [2:0] SW
);

  wire Clk_out, ratedivider_1_counter_out, shiftregister_1_ledr0;
  wire [13:0] lut_1_lut_out;

  Clock Clk (.out(Clk_out));
  RateDivider ratedivider_1 (.enable(1'b1), .clear(KEY0), .Clk(Clk_out), .counter_out(ratedivider_1_counter_out));
  LUT lut_1 (.SW(SW), .LUT_out(lut_1_lut_out));
  LED led_1 (.in(shiftregister_1_ledr0));
  ShiftRegister shiftregister_1 (
    .Reset(KEY0), .Enable(KEY1), .Clk(ratedivider_1_counter_out), .LUT_out(lut_1_lut_out),
    .LEDR0(shiftregister_1_ledr0));
endmodule

module LUT (
  input  [2:0] SW,
  output [13:0] LUT_out
);

  Multiplexer #(.select(3), .width(14)) multiplexer_1 (
    .in0(14'h2a00), .in1(14'h3800), .in2(14'h2b80), .in3(14'h2ae0), .in4(14'h2ee0), .in5(14'h3ab8),
    .in6(14'h3aee), .in7(14'h3ba8), .out(LUT_out), .sel(SW));
endmodule

module RateDivider (
  input  enable,
  input  clear,
  input  Clk,
  output counter_out
);

  wire not_1_out, or_1_out;
  wire [2:0] counter_1_q;

  or or_1 (or_1_out, counter_out, not_1_out);
  not not_1 (not_1_out, enable);
  Counter #(.max('h7), .width(3)) counter_1 (
    .clr(clear), .load(or_1_out), .up(1'b1), .clk(Clk), .D(3'b000), .Q(counter_1_q));  // open: count, carry
  and and_1 (counter_out, counter_1_q[0], counter_1_q[1], counter_1_q[2]);
endmodule

module ShiftRegister (
  input  Reset,
  input  Enable,
  input  Clk,
  input  [13:0] LUT_out,
  output LEDR0
);

  wire shift_register_1_p2;

  // Shift_Register #(.length(14)) shift_register_1: pin names not known; wires that end beside it: Reset, shift_register_1_p2, Enable, Clk, 1'b0, LUT_out[0], LUT_out[1], LUT_out[2], LUT_out[3], LUT_out[4], LUT_out[5], LUT_out[6], LUT_out[7], LUT_out[8], LUT_out[9], LUT_out[10], LUT_out[11]
  not not_1 (shift_register_1_p2, Enable);
endmodule
